# Fritzing sketch CS 207 Project Breadboard (saved by Fritzing 0.9.5d)
breadboards: 1

parts:
  R1 = Slide Potentiometer [maximum_resistance=100kΩ]
  R2 = Slide Potentiometer [maximum_resistance=100kΩ]
  R3 = Slide Potentiometer [maximum_resistance=100kΩ]
  R4 = Slide Potentiometer [maximum_resistance=100kΩ]
  R5 = Slide Potentiometer [maximum_resistance=100kΩ]
  R6 = Slide Potentiometer [maximum_resistance=100kΩ]
  Part1 = Arduino Uno (Rev3) - ICSP
  R7 = Resistor [tolerance=±5% resistance=560 package=THT]
  R8 = Resistor [tolerance=±5% resistance=560 package=THT]
  R9 = Resistor [tolerance=±5% resistance=560 package=THT]
  R10 = Resistor [tolerance=±5% resistance=560 package=THT]
  R11 = Resistor [tolerance=±5% resistance=560 package=THT]
  R12 = Resistor [tolerance=±5% resistance=560 package=THT]

nets:
  N1: R1.leg1, R8.Pin_0
  N2: R1.wiper, Part1.A5/SCL
  N3: R1.leg2, R2.leg2, R3.leg2, R4.leg2, R5.leg2, R6.leg2, Part1.GND
  N4: R2.leg1, R11.Pin_0
  N5: R2.wiper, Part1.A2
  N6: R3.leg1, R12.Pin_0
  N7: R3.wiper, Part1.A1
  N8: R4.leg1, R7.Pin_0
  N9: R4.wiper, Part1.A0
  N10: R5.leg1, R10.Pin_0
  N11: R5.wiper, Part1.A3
  N12: R6.leg1, R9.Pin_0
  N13: R6.wiper, Part1.A4/SDA
  N14: Part1.5V, R7.Pin_1, R8.Pin_1, R9.Pin_1, R10.Pin_1, R11.Pin_1, R12.Pin_1
