# Fritzing sketch CS Project Schematic (saved by Fritzing 0.9.5d)
breadboards: 1

parts:
  Arduino_Uno = Arduino Uno (Rev3)
  Pot_3 = SLIDER [package=slider]
  Pot_4 = SLIDER [package=slider]
  Pot_0 = SLIDER [package=slider]
  Pot_1 = SLIDER [package=slider]
  Pot_2 = SLIDER [package=slider]
  Pot_5 = SLIDER [package=slider]
  R1 = Resistor [tolerance=±5% resistance=560 package=THT]
  R2 = Resistor [tolerance=±5% resistance=560 package=THT]
  R3 = Resistor [tolerance=±5% resistance=560 package=THT]
  R4 = Resistor [tolerance=±5% resistance=560 package=THT]
  R5 = Resistor [tolerance=±5% resistance=560 package=THT]
  R6 = Resistor [tolerance=±5% resistance=560 package=THT]

nets:
  N1: Arduino_Uno.A0, Pot_0.S
  N2: Arduino_Uno.A1, Pot_1.S
  N3: Arduino_Uno.A2, Pot_2.S
  N4: Arduino_Uno.A3, Pot_3.S
  N5: Arduino_Uno.A4/SDA, Pot_4.S
  N6: Arduino_Uno.A5/SCL, Pot_5.S
  5V: Arduino_Uno.5V, R1.Pin_0, R2.Pin_0, R3.Pin_0, R4.Pin_0, R5.Pin_0, R6.Pin_0
  GND: Arduino_Uno.GND, Pot_3.A, Pot_4.A, Pot_0.A, Pot_1.A, Pot_2.A, Pot_5.A
